# Fritzing sketch eye (saved by Fritzing 0.9.3b)
breadboards: 1

parts:
  PWM1 = PCA9685 16x12-bit PWM Breakout
  Componente1 = Arduino Uno (Rev3) - ICSP
  SERVO1 = Tower Pro SG90 servo [part_number=101246]
  R1 = Rotary Potentiometer (Large) [maximum_resistance=100kΩ package=THT]
  S3 = Pushbutton [package="[THT]"]
  R2 = Resistor [tolerance=±5% resistance=10k package=THT]
  JACK2 = 2.1mm Barrel Jack with Terminal Block
  Componente3 = Black Joystick KY-023

nets:
  N1: PWM1.no_name_yet#0, SERVO1.Signal
  N2: PWM1.no_name_yet#100, PWM1.no_name_yet#706, SERVO1.+5V, JACK2.POS
  GND: PWM1.no_name_yet#501, PWM1.no_name_yet#701, PWM1.no_name_yet#1000, Componente1.GND, SERVO1.GND, R1.leg1, R2.Pin_0, JACK2.NEG, Componente3.GND
  N3: PWM1.no_name_yet#503, Componente1.A4/SDA
  N4: PWM1.no_name_yet#504, Componente1.A5/SCL
  5V: PWM1.no_name_yet#505, Componente1.D2, Componente1.5V, R1.leg2, S3.Pin_1, S3.Pin_2, R2.Pin_1, Componente3.+5V
  N5: Componente1.A0, Componente3.VRy
  N6: Componente1.A1, Componente3.VRx
  N7: Componente1.A2, R1.wiper
  N8: S3.Pin_3, S3.Pin_4

notes:
  External +5V
  10K
  orange (PWM)
  red (+5V)
  brown (GND)
  joystick
  potentiometer
  button
  Adafruit PCA9685 PWM Servo
  SG90 Micro Servos

custom parts:
  Tower Pro SG90 servo: Original file by John De Cristofaro http://www.adafruit.com/products/1449 Adafruit Feedback Servo (Small) Edited by: e-radionica.com 28/9/2015
  Black Joystick KY-023: Description: The joystick is a combination of 2 analoog potentiometer and a digital switch. Arduino GND --> Module pin - Arduino +5V --> Module pin +5V Arduino Analoog 0 --> Module VRx Arduino Analoog 1 --> Module VRy Arduino Digital --> Module SW Dimensions: 1" x 1.25"
